// Digital circuit CU.dig as structural Verilog
module CU (
  input  [3:0] Opcode__IR,
  input  Zero_flag,
  input  reset,
  input  clock,
  output [2:0] ALU_Op,
  output [1:0] Read_Reg_1,
  output [1:0] Read_Reg_2,
  output [1:0] Write_Reg,
  output Write_Enabled,
  output Immediate_Load,
  output Increment,
  output Fetch_Enable
);

  wire and_1_out, and_2_out, and_3_out, and_4_out, not_2_out, not_3_out, not_4_out, not_5_out, not_6_out,
       not_7_out, not_8_out, not_9_out, not_10_out, not_11_out, not_12_out, not_13_out, not_14_out,
       not_15_out, not_16_out, not_17_out;
  wire [2:0] and_11_out, and_12_out, and_13_out, and_14_out, and_15_out, and_16_out;
  wire [2:2] and_5_out, and_6_out, and_7_out, and_8_out, and_9_out, and_10_out;

  not not_1 (Read_Reg_1[0], Opcode__IR[0]);
  not not_2 (not_2_out, Opcode__IR[0]);
  not not_3 (not_3_out, Opcode__IR[1]);
  not not_4 (not_4_out, Opcode__IR[1]);
  not not_5 (not_5_out, Opcode__IR[2]);
  not not_6 (not_6_out, Opcode__IR[3]);
  not not_7 (not_7_out, Opcode__IR[0]);
  not not_8 (not_8_out, Opcode__IR[0]);
  and and_1 (and_1_out, not_2_out, not_3_out, Opcode__IR[2]);
  and and_2 (and_2_out, not_4_out, not_5_out, not_6_out);
  or or_1 (Write_Enabled, Opcode__IR[0], Opcode__IR[2], Opcode__IR[3]);
  and and_3 (and_3_out, not_7_out, Opcode__IR[3]);
  and and_4 (and_4_out, not_8_out, Opcode__IR[2]);
  not not_9 (not_9_out, Opcode__IR[1]);
  not not_10 (not_10_out, Opcode__IR[2]);
  not not_11 (not_11_out, Opcode__IR[1]);
  not not_12 (not_12_out, Opcode__IR[3]);
  not not_13 (not_13_out, Opcode__IR[1]);
  not not_14 (not_14_out, Opcode__IR[2]);
  not not_15 (not_15_out, Opcode__IR[3]);
  not not_16 (not_16_out, Opcode__IR[2]);
  not not_17 (not_17_out, Opcode__IR[3]);
  or or_2 (Fetch_Enable, and_1_out, and_2_out);
  or or_3 (Immediate_Load, and_3_out, and_4_out);
  and and_5 (and_5_out[2], Opcode__IR[0], not_9_out, not_10_out, Opcode__IR[3]);
  and and_6 (and_6_out[2], Opcode__IR[0], not_11_out, Opcode__IR[2], not_12_out);
  and and_7 (and_7_out[2], Opcode__IR[0], not_13_out, Opcode__IR[2], Opcode__IR[3]);
  and and_8 (and_8_out[2], Opcode__IR[0], Opcode__IR[1], not_14_out, not_15_out);
  and and_9 (and_9_out[2], Opcode__IR[0], Opcode__IR[1], not_16_out, Opcode__IR[3]);
  and and_10 (and_10_out[2], Opcode__IR[0], Opcode__IR[1], Opcode__IR[2], not_17_out);
  assign and_11_out = {3{Fetch_Enable}} & {3{and_5_out[2]}};  // And and_11, 3 bits wide
  assign and_12_out = {{2{Fetch_Enable}}, 1'b1} & {3{and_6_out[2]}};  // And and_12, 3 bits wide
  assign and_13_out = {Fetch_Enable, 1'b1, Fetch_Enable} & {3{and_7_out[2]}};  // And and_13, 3 bits wide
  assign and_14_out = {Fetch_Enable, 2'b11} & {3{and_8_out[2]}};  // And and_14, 3 bits wide
  assign and_15_out = {1'b1, {2{Fetch_Enable}}} & {3{and_9_out[2]}};  // And and_15, 3 bits wide
  assign and_16_out = {1'b1, Fetch_Enable, 1'b1} & {3{and_10_out[2]}};  // And and_16, 3 bits wide
  assign ALU_Op = and_11_out ^ and_12_out ^ and_13_out ^ and_14_out ^ and_15_out ^ and_16_out;  // XOr xor_1, 3 bits wide

  assign Increment = Fetch_Enable;
  assign Read_Reg_1[1] = Fetch_Enable;
  assign Read_Reg_2 = {Fetch_Enable, 1'b1};
  assign Write_Reg = {2{Fetch_Enable}};
  // also tied to GND on the sheet: Fetch_Enable
endmodule
